// Logisim project processor.circ as structural Verilog: 7 circuits, main circuit main
module main (
  input  [31:0] Instruction,
  input  in_2,
  input  in_3,
  input  in_4,
  input  [1:0] in_5,
  input  [31:0] data1,
  input  in_7,
  input  [31:0] data2,
  output [31:0] out_9
);

  wire clock_1_out, not_1_out, not_2_out, not_3_out;
  wire [3:0] decode_1_out_2;
  wire [4:0] FUNCT3, RD, register_3_q, register_5_q, register_6_q, register_11_q, RS1, RS2;
  wire [5:0] FUNCT7, OPCODE, register_7_q;
  wire [31:0] alu_1_out_4, ram_1_data, ram_2_data, register_1_q, register_8_q, register_9_q, register_10_q,
       register_12_q;

  MEM mem_1 ();  // open: Address, Write_Data, WriteEn, clk, Read_Data
  Clock clock_1 (.out(clock_1_out));
  Register #(.width(32)) register_1 (.D(Instruction), .Q(register_1_q), .clk(clock_1_out));  // open: en, clr
  IF if_1 (
    .Instruction(register_1_q), .in_2(in_5), .OPCODE(OPCODE), .RD(RD), .FUNCT3(FUNCT3), .RS1(RS1), .RS2(RS2),
    .FUNCT7(FUNCT7));
  Register #(.width(6)) register_2 (.D(OPCODE), .clk(clock_1_out));  // open: en, Q, clr
  Register #(.width(5)) register_3 (.D(RD), .Q(register_3_q), .clk(clock_1_out));  // open: en, clr
  Register #(.width(5)) register_4 (.D(FUNCT3), .clk(clock_1_out));  // open: en, Q, clr
  Register #(.width(5)) register_5 (.D(RS1), .Q(register_5_q), .clk(clock_1_out));  // open: en, clr
  Register #(.width(5)) register_6 (.D(RS2), .Q(register_6_q), .clk(clock_1_out));  // open: en, clr
  Register #(.width(6)) register_7 (.D(FUNCT7), .Q(register_7_q), .clk(clock_1_out));  // open: en, clr
  Register #(.width(32)) register_8 (.D(data1), .Q(register_8_q), .clk(clock_1_out));  // open: en, clr
  Register #(.width(32)) register_9 (.D(data2), .Q(register_9_q), .clk(clock_1_out));  // open: en, clr
  Decode decode_1 (.in_1(register_7_q), .out_2(decode_1_out_2));
  not not_1 (not_1_out, in_4);
  not not_2 (not_2_out, in_7);
  RAM #(.addrWidth(5), .dataWidth(32), .bus("separate")) ram_1 (
    .addr(register_5_q), .din(register_8_q), .data(ram_1_data), .str(not_1_out), .clk(clock_1_out),
    .ld(not_1_out));  // open: sel, clr
  RAM #(.addrWidth(5), .dataWidth(32), .bus("separate")) ram_2 (
    .addr(register_6_q), .din(register_9_q), .data(ram_2_data), .str(not_2_out), .clk(clock_1_out),
    .ld(not_2_out));  // open: sel, clr
  ALU alu_1 (.RS1(ram_1_data), .RS2(ram_2_data), .SELECTOR(decode_1_out_2), .out_4(alu_1_out_4));
  Register #(.width(32)) register_10 (.D(alu_1_out_4), .Q(register_10_q), .clk(clock_1_out));  // open: en, clr
  Register #(.width(5)) register_11 (.D(register_3_q), .Q(register_11_q), .clk(clock_1_out));  // open: en, clr
  Register #(.width(32)) register_12 (.D(register_10_q), .Q(register_12_q), .clk(clock_1_out));  // open: en, clr
  not not_3 (not_3_out, in_2);
  RAM #(.addrWidth(5), .dataWidth(32), .bus("separate")) ram_3 (
    .addr(register_11_q), .din(register_12_q), .data(out_9), .str(not_3_out), .clk(clock_1_out),
    .ld(not_3_out), .clr(in_3));  // open: sel
  Register #(.width(5)) register_13 (.D(register_11_q), .clk(clock_1_out));  // open: en, Q, clr
  Register #(.width(32)) register_14 (.D(out_9), .clk(clock_1_out));  // open: en, Q, clr

  // Other names for the same wires on the sheet: R_I_J_TYPE[1:0] = in_5
endmodule

// Arithmetic Logic Unit
module ALU (
  input  [31:0] RS1,
  input  [31:0] RS2,
  input  [3:0] SELECTOR,
  output [31:0] out_4
);

  wire comparator_1_eq, comparator_1_gt, comparator_1_lt;
  wire [31:0] adder_1_out, and_1_out, bit_extender_1_out, bit_extender_2_out, bit_extender_3_out,
       divider_1_out, multiplier_1_out, or_1_out, shifter_1_out, shifter_2_out, shifter_3_out,
       subtractor_1_out, xor_1_out;

  Adder #(.width(32)) adder_1 (.a(RS1), .b(RS2), .out(adder_1_out));  // open: cin, cout
  Subtractor #(.width(32)) subtractor_1 (.a(RS1), .b(RS2), .out(subtractor_1_out));  // open: bin, bout
  Multiplier #(.width(32)) multiplier_1 (.a(RS1), .b(RS2), .out(multiplier_1_out));  // open: cin, cout
  Divider #(.width(32)) divider_1 (.a(RS1), .b(RS2), .out(divider_1_out));  // open: upper, rem
  assign and_1_out = RS1 & RS2;  // AND_Gate and_1, 32 bits wide
  assign xor_1_out = RS1 ^ RS2;  // XOR_Gate xor_1, 32 bits wide
  assign or_1_out = RS1 | RS2;  // OR_Gate or_1, 32 bits wide
  Comparator #(.width(32)) comparator_1 (
    .a(RS1), .b(RS2), .gt(comparator_1_gt), .eq(comparator_1_eq), .lt(comparator_1_lt));
  Shifter #(.width(32)) shifter_1 (.in(RS1), .\dist (RS2[4:0]), .out(shifter_1_out));
  Shifter #(.width(32)) shifter_2 (.in(RS1), .\dist (RS2[4:0]), .out(shifter_2_out));
  Shifter #(.width(32), .shift("ar")) shifter_3 (.in(RS1), .\dist (RS2[4:0]), .out(shifter_3_out));
  assign bit_extender_1_out = {{31{1'b0}}, comparator_1_gt};  // Bit_Extender bit_extender_1
  assign bit_extender_2_out = {{31{1'b0}}, comparator_1_eq};  // Bit_Extender bit_extender_2
  assign bit_extender_3_out = {{31{1'b0}}, comparator_1_lt};  // Bit_Extender bit_extender_3
  Multiplexer #(.select(4), .width(32)) multiplexer_1 (
    .in0(adder_1_out), .in1(subtractor_1_out), .in2(multiplier_1_out), .in3(divider_1_out), .in4(and_1_out),
    .in5(xor_1_out), .in6(or_1_out), .in7(bit_extender_1_out), .in8(bit_extender_2_out),
    .in9(bit_extender_3_out), .in10(shifter_1_out), .in11(shifter_2_out), .in12(shifter_3_out), .in13(RS2),
    .out(out_4), .sel(SELECTOR));  // open: in14, in15, en

  // Other names for the same wires on the sheet: bsel[31:0] = RS2
endmodule

module Decode (
  input  [5:0] in_1,
  output [3:0] out_2
);

  Bit_Extender #(.in_width(6), .out_width(4)) bit_extender_1 (.in(in_1), .out(out_2));

  // Other names for the same wires on the sheet: Funct7_ID[5:0] = in_1
endmodule

module IF (
  input  [31:0] Instruction,
  input  [1:0] in_2,
  output [5:0] OPCODE,
  output [4:0] RD,
  output [4:0] FUNCT3,
  output [4:0] RS1,
  output [4:0] RS2,
  output [5:0] FUNCT7
);

  Multiplexer #(.select(2), .width(6)) multiplexer_1 (
    .in0(Instruction[5:0]), .out(OPCODE), .sel(in_2));  // open: in1, in2, in3, en
  Multiplexer #(.select(2), .width(5)) multiplexer_2 (
    .in0(Instruction[10:6]), .out(RD), .sel(in_2));  // open: in1, in2, in3, en
  Multiplexer #(.select(2), .width(5)) multiplexer_3 (
    .in0(Instruction[15:11]), .out(FUNCT3), .sel(in_2));  // open: in1, in2, in3, en
  Multiplexer #(.select(2), .width(5)) multiplexer_4 (
    .in0(Instruction[20:16]), .out(RS1), .sel(in_2));  // open: in1, in2, in3, en
  Multiplexer #(.select(2), .width(5)) multiplexer_5 (
    .in0(Instruction[25:21]), .out(RS2), .sel(in_2));  // open: in1, in2, in3, en
  Multiplexer #(.select(2), .width(6)) multiplexer_6 (
    .in0(Instruction[31:26]), .out(FUNCT7), .sel(in_2));  // open: in1, in2, in3, en
  // Probe on nothing
endmodule

module Register_File (
  input  [31:0] in_1,
  input  [31:0] in_2,
  input  [3:0] RS1,
  input  [3:0] RS2,
  input  [3:0] RD,
  output [31:0] RS1_2,
  output [31:0] RS2_2,
  output [31:0] RD_2
);

  wire clock_1_out, R0_En, R1_En, R2_En, R3_En, R4_En, R5_En, R6_En, R7_En;
  wire [31:0] R0, R1, R2, R3, R4, R5, R6, R7;

  Demultiplexer #(.select(4)) demultiplexer_1 (
    .out0(R0_En), .out1(R1_En), .out2(R2_En), .out3(R3_En), .out4(R4_En), .out5(R5_En), .out6(R6_En),
    .out7(R7_En), .in(1'b1), .sel(RS1));  // open: out8, out9, out10, out11, out12, out13, out14, out15, en
  Demultiplexer #(.select(4)) demultiplexer_2 (
    .out0(R0_En), .out1(R1_En), .out2(R2_En), .out3(R3_En), .out4(R4_En), .out5(R5_En), .out6(R6_En),
    .out7(R7_En), .in(1'b1), .sel(RS2));  // open: out8, out9, out10, out11, out12, out13, out14, out15, en
  Demultiplexer #(.select(4)) demultiplexer_3 (
    .out0(R0_En), .out1(R1_En), .out2(R2_En), .out3(R3_En), .out4(R4_En), .out5(R5_En), .out6(R6_En),
    .out7(R7_En), .in(1'b1), .sel(RD));  // open: out8, out9, out10, out11, out12, out13, out14, out15, en
  Register #(.width(32)) u_R0 (.en(R0_En), .Q(R0), .clk(clock_1_out));  // open: D, clr
  Register #(.width(32)) u_R1 (.en(R1_En), .Q(R1), .clk(clock_1_out));  // open: D, clr
  Register #(.width(32)) u_R2 (.en(R2_En), .Q(R2), .clk(clock_1_out));  // open: D, clr
  Register #(.width(32)) u_R3 (.en(R3_En), .Q(R3), .clk(clock_1_out));  // open: D, clr
  Register #(.width(32)) u_R4 (.en(R4_En), .Q(R4), .clk(clock_1_out));  // open: D, clr
  Register #(.width(32)) u_R5 (.en(R5_En), .Q(R5), .clk(clock_1_out));  // open: D, clr
  Register #(.width(32)) u_R6 (.en(R6_En), .Q(R6), .clk(clock_1_out));  // open: D, clr
  Register #(.width(32)) u_R7 (.en(R7_En), .Q(R7), .clk(clock_1_out));  // open: D, clr
  Clock clock_1 (.out(clock_1_out));
  Multiplexer #(.select(4), .width(32)) multiplexer_1 (
    .in0(R0), .in1(R1), .in2(R2), .in3(R3), .in4(R4), .in5(R5), .in6(R6), .in7(R7), .out(RS1_2), .sel(RS1));  // open: in8, in9, in10, in11, in12, in13, in14, in15, en
  Multiplexer #(.select(4), .width(32)) multiplexer_2 (
    .in0(R0), .in1(R1), .in2(R2), .in3(R3), .in4(R4), .in5(R5), .in6(R6), .in7(R7), .out(RS2_2), .sel(RS2));  // open: in8, in9, in10, in11, in12, in13, in14, in15, en
  Multiplexer #(.select(4), .width(32)) multiplexer_3 (
    .in0(R0), .in1(R1), .in2(R2), .in3(R3), .in4(R4), .in5(R5), .in6(R6), .in7(R7), .out(RD_2), .sel(RD));  // open: in8, in9, in10, in11, in12, in13, in14, in15, en

  // Other names for the same wires on the sheet: R1_Data[31:0] = in_1; R2_Data[31:0] = in_2
endmodule

module Control (
  input  [31:0] Instruction,
  input  BRLT,
  input  BREQ,
  output A_Sel,
  output B_Sel,
  output MemRW,
  output RWEn,
  output PC_Sel
);

  wire and_1_out, branch, comparator_1_eq, comparator_2_eq, comparator_3_eq, comparator_5_eq,
       comparator_6_eq, comparator_7_eq, comparator_8_eq;

  or or_1 (branch, BRLT, BREQ);
  Comparator #(.width(7)) comparator_1 (.a(Instruction[6:0]), .b(7'b0110011), .eq(comparator_1_eq));  // open: gt, lt
  Comparator #(.width(7)) comparator_2 (.a(Instruction[6:0]), .b(7'b0000011), .eq(comparator_2_eq));  // open: gt, lt
  Comparator #(.width(7)) comparator_3 (.a(Instruction[6:0]), .b(7'b0010011), .eq(comparator_3_eq));  // open: gt, lt
  Comparator #(.width(7)) comparator_4 (.a(Instruction[6:0]), .b(7'b0100011), .eq(MemRW));  // open: gt, lt
  Comparator #(.width(7)) comparator_5 (.a(Instruction[6:0]), .b(7'b0110111), .eq(comparator_5_eq));  // open: gt, lt
  Comparator #(.width(7)) comparator_6 (.a(Instruction[6:0]), .b(7'b1100011), .eq(comparator_6_eq));  // open: gt, lt
  Comparator #(.width(7)) comparator_7 (.a(Instruction[6:0]), .b(7'b1101111), .eq(comparator_7_eq));  // open: gt, lt
  Comparator #(.width(7)) comparator_8 (.a(Instruction[6:0]), .b(7'b1100111), .eq(comparator_8_eq));  // open: gt, lt
  and and_1 (and_1_out, branch, comparator_6_eq);
  or or_2 (A_Sel, comparator_1_eq, comparator_2_eq, comparator_3_eq, MemRW, comparator_8_eq);
  or or_3 (B_Sel, comparator_2_eq, comparator_3_eq, comparator_5_eq, comparator_6_eq, comparator_7_eq, comparator_8_eq);
  or or_4 (RWEn, MemRW, comparator_6_eq);
  or or_5 (PC_Sel, and_1_out, comparator_7_eq, comparator_8_eq);

  // Other names for the same wires on the sheet: Opcode[6:0] = Instruction[6:0]; Funct3[2:0] = Instruction[14:12]
endmodule

module MEM (
  input  [31:0] Address,
  input  [31:0] Write_Data,
  input  WriteEn,
  input  clk,
  output [31:0] Read_Data
);

  wire and_1_out;

  buf and_1 (and_1_out, clk);  // AND_Gate
  RAM #(.addrWidth(14), .dataWidth(32), .bus("separate")) ram_1 (
    .addr(Address[15:2]), .din(Write_Data), .data(Read_Data), .str(WriteEn), .sel(1'b1), .clk(and_1_out),
    .ld(1'b1));  // open: clr
endmodule
